# Fritzing sketch sketch (saved by Fritzing 1.0.1rc)

parts:
  U1 = JST XH 4A 2.54mm [mn=dfgvfd mpn=gdfgsdf part_number=gsdfg package=THT]
  A1 = Waveshare rp2040-zero tht extra conns [package=THT]
  U2 = JST XH 4A 2.54mm [package=THT]

nets:
  N1: U1.pin1, A1.Pin_2, A1.Pin_33, U2.pin1
  N2: U1.pin3, A1.Pin_23
  N3: U1.pin4, A1.Pin_22
  N4: A1.Pin_20, U2.pin4
  N5: A1.Pin_21, U2.pin3

notes:
  device B
  SCL
  SDA
  GND
  device A

custom parts:
  JST XH 4A 2.54mm: 4 Pin JST XH connector
  Waveshare rp2040-zero tht extra conns: .RP2040-Zero, A Low-Cost, High-Performance Pico-Like MCU Board Based On Raspberry Pi Microcontroller RP2040. This varant is THT with the extra connections.
